// Logisim project Main_Project.circ as structural Verilog
module _1_bit_Alu (
  input  cin,
  input  A,
  input  Ainv,
  input  B,
  input  Binv,
  input  [1:0] Alu_Op,
  output S,
  output cout
);

  wire adder_1_out, and_1_out, multiplexer_1_out, multiplexer_2_out, not_1_out, not_2_out, or_1_out,
       xor_1_out;

  not not_1 (not_1_out, A);
  not not_2 (not_2_out, B);
  Multiplexer multiplexer_1 (.in0(A), .in1(not_1_out), .out(multiplexer_1_out), .sel(Ainv));  // open: en
  Multiplexer multiplexer_2 (.in0(B), .in1(not_2_out), .out(multiplexer_2_out), .sel(Binv));  // open: en
  and and_1 (and_1_out, multiplexer_1_out, multiplexer_2_out);
  or or_1 (or_1_out, multiplexer_1_out, multiplexer_2_out);
  Adder #(.width(1)) adder_1 (.a(multiplexer_1_out), .b(multiplexer_2_out), .out(adder_1_out), .cin(cin), .cout(cout));
  xor xor_1 (xor_1_out, multiplexer_1_out, multiplexer_2_out);
  Multiplexer #(.select(2)) multiplexer_3 (
    .in0(and_1_out), .in1(or_1_out), .in2(adder_1_out), .in3(xor_1_out), .out(S), .sel(Alu_Op));  // open: en
endmodule

module _12_bit_Alu (
  input  [11:0] A,
  input  [1:0] Op,
  input  Cin,
  input  A_inv,
  input  B_inv,
  input  [11:0] B,
  output [11:0] out_7,
  output Zero,
  output OverFlow,
  output Cout
);

  wire n1_bit_alu_1_cout, n1_bit_alu_2_cout, n1_bit_alu_3_cout, n1_bit_alu_4_cout, n1_bit_alu_5_cout,
       n1_bit_alu_6_cout, n1_bit_alu_7_cout, n1_bit_alu_8_cout, n1_bit_alu_9_cout, n1_bit_alu_10_cout,
       n1_bit_alu_11_cout;

  _1_bit_Alu u_1_bit_alu_1 (
    .A(A[0]), .Ainv(A_inv), .B(B[0]), .Binv(B_inv), .S(out_7[0]), .cin(Cin), .cout(n1_bit_alu_1_cout),
    .Alu_Op(Op));
  _1_bit_Alu u_1_bit_alu_2 (
    .A(A[1]), .Ainv(A_inv), .B(B[1]), .Binv(B_inv), .S(out_7[1]), .cin(n1_bit_alu_1_cout),
    .cout(n1_bit_alu_2_cout), .Alu_Op(Op));
  _1_bit_Alu u_1_bit_alu_3 (
    .A(A[2]), .Ainv(A_inv), .B(B[2]), .Binv(B_inv), .S(out_7[2]), .cin(n1_bit_alu_2_cout),
    .cout(n1_bit_alu_3_cout), .Alu_Op(Op));
  _1_bit_Alu u_1_bit_alu_4 (
    .A(A[3]), .Ainv(A_inv), .B(B[3]), .Binv(B_inv), .S(out_7[3]), .cin(n1_bit_alu_3_cout),
    .cout(n1_bit_alu_4_cout), .Alu_Op(Op));
  _1_bit_Alu u_1_bit_alu_5 (
    .A(A[4]), .Ainv(A_inv), .B(B[4]), .Binv(B_inv), .S(out_7[4]), .cin(n1_bit_alu_4_cout),
    .cout(n1_bit_alu_5_cout), .Alu_Op(Op));
  _1_bit_Alu u_1_bit_alu_6 (
    .A(A[5]), .Ainv(A_inv), .B(B[5]), .Binv(B_inv), .S(out_7[5]), .cin(n1_bit_alu_5_cout),
    .cout(n1_bit_alu_6_cout), .Alu_Op(Op));
  _1_bit_Alu u_1_bit_alu_7 (
    .A(A[6]), .Ainv(A_inv), .B(B[6]), .Binv(B_inv), .S(out_7[6]), .cin(n1_bit_alu_6_cout),
    .cout(n1_bit_alu_7_cout), .Alu_Op(Op));
  _1_bit_Alu u_1_bit_alu_8 (
    .A(A[7]), .Ainv(A_inv), .B(B[7]), .Binv(B_inv), .S(out_7[7]), .cin(n1_bit_alu_7_cout),
    .cout(n1_bit_alu_8_cout), .Alu_Op(Op));
  _1_bit_Alu u_1_bit_alu_9 (
    .A(A[8]), .Ainv(A_inv), .B(B[8]), .Binv(B_inv), .S(out_7[8]), .cin(n1_bit_alu_8_cout),
    .cout(n1_bit_alu_9_cout), .Alu_Op(Op));
  _1_bit_Alu u_1_bit_alu_10 (
    .A(A[9]), .Ainv(A_inv), .B(B[9]), .Binv(B_inv), .S(out_7[9]), .cin(n1_bit_alu_9_cout),
    .cout(n1_bit_alu_10_cout), .Alu_Op(Op));
  _1_bit_Alu u_1_bit_alu_11 (
    .A(A[10]), .Ainv(A_inv), .B(B[10]), .Binv(B_inv), .S(out_7[10]), .cin(n1_bit_alu_10_cout),
    .cout(n1_bit_alu_11_cout), .Alu_Op(Op));
  _1_bit_Alu u_1_bit_alu_12 (
    .A(A[11]), .Ainv(A_inv), .B(B[11]), .Binv(B_inv), .S(out_7[11]), .cin(n1_bit_alu_11_cout), .cout(Cout),
    .Alu_Op(Op));
  xor xor_1 (OverFlow, n1_bit_alu_11_cout, Cout);
  nor nor_1 (Zero, out_7[0], out_7[1], out_7[2], out_7[3], out_7[4], out_7[5], out_7[6], out_7[7], out_7[8], out_7[9], out_7[10], out_7[11]);

  // Other names for the same wires on the sheet: Res0 = out_7[0]; Res1 = out_7[1]; Res2 = out_7[2]; Res3 = out_7[3];
  //   Res4 = out_7[4]; Res5 = out_7[5]; Res6 = out_7[6]; Res7 = out_7[7]; Res8 = out_7[8]; Res9 = out_7[9];
  //   Res10 = out_7[10]; Res11 = out_7[11]

  // Notes on the sheet:
  //   Res
endmodule

module _12_bit_Register (
  input  Write_Enable,
  input  [11:0] Write_Data,
  input  CLK,
  input  [2:0] RD,
  input  [2:0] RS,
  input  [2:0] RT,
  output [11:0] out_7,
  output [11:0] out_8
);

  wire and_1_out, and_2_out, and_3_out, and_4_out, and_5_out, and_6_out, and_7_out, and_8_out,
       decoder_1_out0, decoder_1_out1, decoder_1_out2, decoder_1_out3, decoder_1_out4, decoder_1_out5,
       decoder_1_out6, decoder_1_out7;
  wire [11:0] R0_q, R1_q, R2_q, R3_q, R4_q, R5_q, R6_q, R7_q;

  and and_1 (and_1_out, decoder_1_out0, Write_Enable);
  and and_2 (and_2_out, decoder_1_out1, Write_Enable);
  Register #(.width(12)) R0 (.D(Write_Data), .en(and_1_out), .Q(R0_q), .clk(CLK));  // open: clr
  Decoder #(.select(3), .enable("false")) decoder_1 (
    .out0(decoder_1_out0), .out1(decoder_1_out1), .out2(decoder_1_out2), .out3(decoder_1_out3),
    .out4(decoder_1_out4), .out5(decoder_1_out5), .out6(decoder_1_out6), .out7(decoder_1_out7), .sel(RD));
  and and_3 (and_3_out, decoder_1_out2, Write_Enable);
  Register #(.width(12)) R1 (.D(Write_Data), .en(and_2_out), .Q(R1_q), .clk(CLK));  // open: clr
  Multiplexer #(.select(3), .width(12)) multiplexer_1 (
    .in0(R0_q), .in1(R1_q), .in2(R2_q), .in3(R3_q), .in4(R4_q), .in5(R5_q), .in6(R6_q), .in7(R7_q),
    .out(out_7), .sel(RS));  // open: en
  and and_4 (and_4_out, decoder_1_out4, Write_Enable);
  and and_5 (and_5_out, decoder_1_out3, Write_Enable);
  Register #(.width(12)) R2 (.D(Write_Data), .en(and_3_out), .Q(R2_q), .clk(CLK));  // open: clr
  Register #(.width(12)) R3 (.D(Write_Data), .en(and_5_out), .Q(R3_q), .clk(CLK));  // open: clr
  and and_6 (and_6_out, decoder_1_out5, Write_Enable);
  Register #(.width(12)) R4 (.D(Write_Data), .en(and_4_out), .Q(R4_q), .clk(CLK));  // open: clr
  and and_7 (and_7_out, decoder_1_out6, Write_Enable);
  Register #(.width(12)) R5 (.D(Write_Data), .en(and_6_out), .Q(R5_q), .clk(CLK));  // open: clr
  Multiplexer #(.select(3), .width(12)) multiplexer_2 (
    .in0(R0_q), .in1(R1_q), .in2(R2_q), .in3(R3_q), .in4(R4_q), .in5(R5_q), .in6(R6_q), .in7(R7_q),
    .out(out_8), .sel(RT));  // open: en
  and and_8 (and_8_out, decoder_1_out7, Write_Enable);
  Register #(.width(12)) R7 (.D(Write_Data), .en(and_8_out), .Q(R7_q), .clk(CLK));  // open: clr
  Register #(.width(12)) R6 (.D(Write_Data), .en(and_7_out), .Q(R6_q), .clk(CLK));  // open: clr

  // Notes on the sheet:
  //   Data 1
  //   Data 2
endmodule

module R_type_Datapath (
  input  Ainv,
  input  Binv,
  input  Cin,
  input  [1:0] ALUOP,
  input  WriteEn,
  output [11:0] RT_Value,
  output [11:0] RS_Value,
  output [11:0] RD_Value,
  output [2:0] OPCODE,
  output [2:0] RD,
  output [2:0] RS,
  output [2:0] RT
);

  wire clock_1_out, n12_bit_alu_1_cout, n12_bit_alu_1_overflow, n12_bit_alu_1_zero;
  wire [11:0] adder_1_out, PC_q;

  Register #(.width(12)) PC (.D(adder_1_out), .Q(PC_q), .clk(clock_1_out));  // open: en, clr
  Clock clock_1 (.out(clock_1_out));
  Adder #(.width(12)) adder_1 (.a(12'h1), .b(PC_q), .out(adder_1_out));  // open: cin, cout
  ROM #(.addrWidth(12), .dataWidth(12)) rom_1 (.addr(PC_q), .data({OPCODE, RD, RS, RT}));  // open: sel
  _12_bit_Register u_12_bit_register_1 (
    .Write_Enable(WriteEn), .Write_Data(RD_Value), .CLK(clock_1_out), .RD(RD), .out_7(RT_Value), .RS(RS),
    .RT(RT), .out_8(RS_Value));
  _12_bit_Alu u_12_bit_alu_1 (
    .A(RT_Value), .out_7(RD_Value), .Op(ALUOP), .B(RS_Value), .Zero(n12_bit_alu_1_zero),
    .OverFlow(n12_bit_alu_1_overflow), .A_inv(Ainv), .B_inv(Binv), .Cin(Cin), .Cout(n12_bit_alu_1_cout));
  LED led_1 (.in(n12_bit_alu_1_overflow));
  LED led_2 (.in(n12_bit_alu_1_zero));
  LED led_3 (.in(n12_bit_alu_1_cout));

  // Notes on the sheet:
  //   contents of rom_1 (hex, n*v repeats v):
  //   53 567 567
endmodule

module I_type_Datapath (
  input  Ainv,
  input  Binv,
  input  Cin,
  input  [1:0] ALUOP,
  input  WriteEn,
  output [11:0] RD_in,
  output [11:0] imm,
  output [11:0] RD,
  output [2:0] opcode,
  output [2:0] RT,
  output [2:0] RS,
  output [2:0] IMM_2
);

  wire CLK_out, n12_bit_alu_1_cout, n12_bit_alu_1_overflow, n12_bit_alu_1_zero;
  wire [11:0] adder_1_out, PC_q;

  Register #(.width(12)) PC (.D(adder_1_out), .Q(PC_q), .clk(CLK_out));  // open: en, clr
  Clock CLK (.out(CLK_out));
  Adder #(.width(12)) adder_1 (.a(12'h1), .b(PC_q), .out(adder_1_out));  // open: cin, cout
  ROM #(.addrWidth(12), .dataWidth(12)) rom_1 (.addr(PC_q), .data({opcode, RT, RS, IMM_2}));  // open: sel
  assign imm = {{9{1'b0}}, IMM_2};  // Bit_Extender bit_extender_1
  _12_bit_Register u_12_bit_register_1 (
    .Write_Enable(WriteEn), .Write_Data(RD), .CLK(CLK_out), .RS(RS), .RT(RT), .out_8(RD_in));  // open: RD, out_7
  _12_bit_Alu u_12_bit_alu_1 (
    .A(imm), .out_7(RD), .Op(ALUOP), .B(RD_in), .Zero(n12_bit_alu_1_zero), .OverFlow(n12_bit_alu_1_overflow),
    .A_inv(Ainv), .B_inv(Binv), .Cin(Cin), .Cout(n12_bit_alu_1_cout));
  LED led_1 (.in(n12_bit_alu_1_overflow));
  LED led_2 (.in(n12_bit_alu_1_zero));
  LED led_3 (.in(n12_bit_alu_1_cout));

  // Notes on the sheet:
  //   contents of rom_1 (hex, n*v repeats v):
  //   567 567 567
endmodule

module J_type_Datapath (
  input  in_1,
  output [11:0] Jump_p_Target,
  output [8:0] Jump_p_Target_2,
  output [2:0] OPCODE,
  output [2:0] RD,
  output [2:0] RS,
  output [2:0] RT
);

  wire clock_1_out;
  wire [8:0] adder_1_out;
  wire [11:0] multiplexer_1_out, PC_q;

  Clock clock_1 (.out(clock_1_out));
  Multiplexer #(.width(12), .enable("false")) multiplexer_1 (
    .in0({Jump_p_Target[11:9], adder_1_out}), .in1(Jump_p_Target), .out(multiplexer_1_out), .sel(in_1));
  Register #(.width(12)) PC (.D(multiplexer_1_out), .Q(PC_q), .clk(clock_1_out));  // open: en, clr
  Adder #(.width(12)) adder_1 (.a(12'h1), .b(PC_q), .out({Jump_p_Target[11:9], adder_1_out}));  // open: cin, cout
  ROM #(.addrWidth(12), .dataWidth(12)) rom_1 (.addr(PC_q), .data({OPCODE, Jump_p_Target[8:0]}));  // open: sel

  assign Jump_p_Target_2 = Jump_p_Target[8:0];
  assign RD = Jump_p_Target[8:6];
  assign RS = Jump_p_Target[5:3];
  assign RT = Jump_p_Target[2:0];

  // Notes on the sheet:
  //   contents of rom_1 (hex, n*v repeats v):
  //   5
endmodule

module Lw_datapath (
  input  Ainv,
  input  Binv,
  input  Cin,
  input  [1:0] ALUOP,
  input  WriteEn,
  output [11:0] BASE,
  output [11:0] OFFSET,
  output [11:0] RAM_VALUE,
  output [2:0] opcode,
  output [2:0] DST,
  output [2:0] BASE_2,
  output [2:0] OFFSET_2
);

  wire CLK_out, n12_bit_alu_1_cout, n12_bit_alu_1_overflow, n12_bit_alu_1_zero;
  wire [11:0] adder_1_out, n12_bit_alu_1_out_7, PC_q;

  Register #(.width(12)) PC (.D(adder_1_out), .Q(PC_q), .clk(CLK_out));  // open: en, clr
  Clock CLK (.out(CLK_out));
  Adder #(.width(12)) adder_1 (.a(12'h1), .b(PC_q), .out(adder_1_out));  // open: cin, cout
  ROM #(.addrWidth(12), .dataWidth(12)) rom_1 (.addr(PC_q), .data({opcode, DST, BASE_2, OFFSET_2}));  // open: sel
  _12_bit_Register u_12_bit_register_1 (
    .Write_Enable(WriteEn), .Write_Data(RAM_VALUE), .CLK(CLK_out), .out_7(BASE), .RS(BASE_2), .RT(DST));  // open: RD, out_8
  assign OFFSET = {{9{1'b0}}, OFFSET_2};  // Bit_Extender bit_extender_1
  _12_bit_Alu u_12_bit_alu_1 (
    .A(OFFSET), .out_7(n12_bit_alu_1_out_7), .Op(ALUOP), .B(BASE), .Zero(n12_bit_alu_1_zero),
    .OverFlow(n12_bit_alu_1_overflow), .A_inv(Ainv), .B_inv(Binv), .Cin(Cin), .Cout(n12_bit_alu_1_cout));
  LED led_1 (.in(n12_bit_alu_1_overflow));
  LED led_2 (.in(n12_bit_alu_1_zero));
  LED led_3 (.in(n12_bit_alu_1_cout));
  RAM #(.addrWidth(12), .dataWidth(12)) ram_1 (
    .addr(n12_bit_alu_1_out_7), .data(RAM_VALUE), .ld(1'b1));  // open: sel, clk, clr

  // Notes on the sheet:
  //   contents of rom_1 (hex, n*v repeats v):
  //   567 567 567
endmodule

module SW_Datapath (
  input  Ainv,
  input  Binv,
  input  Cin,
  input  [1:0] ALUOP,
  input  WriteEn,
  output [11:0] BASE,
  output [11:0] OFFSET,
  output [11:0] RAM_VALUE,
  output [2:0] opcode,
  output [2:0] DST,
  output [2:0] BASE_2,
  output [2:0] OFFSET_2
);

  wire CLK_out, n12_bit_alu_1_cout, n12_bit_alu_1_overflow, n12_bit_alu_1_zero;
  wire [11:0] adder_1_out, n12_bit_alu_1_out_7, PC_q;

  Register #(.width(12)) PC (.D(adder_1_out), .Q(PC_q), .clk(CLK_out));  // open: en, clr
  Adder #(.width(12)) adder_1 (.a(12'h1), .b(PC_q), .out(adder_1_out));  // open: cin, cout
  Clock CLK (.out(CLK_out));
  ROM #(.addrWidth(12), .dataWidth(12)) rom_1 (.addr(PC_q), .data({opcode, DST, BASE_2, OFFSET_2}));  // open: sel
  _12_bit_Register u_12_bit_register_1 (
    .Write_Enable(WriteEn), .CLK(CLK_out), .out_7(BASE), .RS(BASE_2), .RT(DST), .out_8(RAM_VALUE));  // open: Write_Data, RD
  assign OFFSET = {{9{1'b0}}, OFFSET_2};  // Bit_Extender bit_extender_1
  _12_bit_Alu u_12_bit_alu_1 (
    .A(OFFSET), .out_7(n12_bit_alu_1_out_7), .Op(ALUOP), .B(BASE), .Zero(n12_bit_alu_1_zero),
    .OverFlow(n12_bit_alu_1_overflow), .A_inv(Ainv), .B_inv(Binv), .Cin(Cin), .Cout(n12_bit_alu_1_cout));
  LED led_1 (.in(n12_bit_alu_1_overflow));
  LED led_2 (.in(n12_bit_alu_1_zero));
  LED led_3 (.in(n12_bit_alu_1_cout));
  RAM #(.addrWidth(12), .dataWidth(12)) ram_1 (
    .addr(n12_bit_alu_1_out_7), .data(RAM_VALUE), .ld(1'b0));  // open: sel, clk, clr

  // Notes on the sheet:
  //   contents of rom_1 (hex, n*v repeats v):
  //   10 121 567
endmodule

module cu (
  input  [2:0] in_1,
  output reg_dst,
  output enable,
  output alu_src,
  output [1:0] out_5,
  output sub,
  output a_inv,
  output sw,
  output lw,
  output ram_to_reg,
  output j
);

  wire and_2_out, and_3_out, and_4_out, and_5_out, and_6_out, and_7_out, not_1_out, not_2_out, not_3_out,
       not_4_out, not_5_out, not_6_out, not_7_out, not_8_out, not_9_out, not_10_out, not_11_out, not_12_out,
       not_13_out, not_14_out, not_15_out, not_16_out, not_17_out, not_18_out;

  not not_1 (not_1_out, in_1[2]);
  not not_2 (not_2_out, in_1[1]);
  not not_3 (not_3_out, in_1[0]);
  not not_4 (not_4_out, in_1[1]);
  not not_5 (not_5_out, in_1[0]);
  not not_6 (not_6_out, in_1[2]);
  not not_7 (not_7_out, in_1[1]);
  not not_8 (not_8_out, in_1[0]);
  not not_9 (not_9_out, in_1[2]);
  not not_10 (not_10_out, in_1[0]);
  not not_11 (not_11_out, in_1[0]);
  not not_12 (not_12_out, in_1[2]);
  not not_13 (not_13_out, in_1[1]);
  not not_14 (not_14_out, in_1[1]);
  not not_15 (not_15_out, in_1[0]);
  not not_16 (not_16_out, in_1[2]);
  not not_17 (not_17_out, in_1[2]);
  and and_1 (j, in_1[2], in_1[1], in_1[0]);
  and and_2 (and_2_out, not_1_out, in_1[1]);
  and and_3 (and_3_out, in_1[2], not_2_out, not_3_out);
  not not_18 (not_18_out, in_1[2]);
  and and_4 (and_4_out, not_4_out, in_1[0]);
  and and_5 (and_5_out, in_1[1], not_5_out);
  and and_6 (and_6_out, not_6_out, in_1[1]);
  and and_7 (and_7_out, in_1[2], not_7_out, not_8_out);
  or or_1 (out_5[1], not_9_out, not_10_out);
  and and_8 (out_5[0], in_1[2], in_1[1], not_11_out);
  and and_9 (sub, not_12_out, not_13_out, in_1[0]);
  and and_10 (sw, in_1[2], not_14_out, not_15_out);
  and and_11 (lw, not_16_out, in_1[1], in_1[0]);
  and and_12 (ram_to_reg, not_17_out, in_1[1], in_1[0]);
  or or_2 (reg_dst, and_2_out, and_3_out);
  or or_3 (enable, not_18_out, and_4_out, and_5_out);
  or or_4 (alu_src, and_6_out, and_7_out);

  assign a_inv = 1'b0;
endmodule

module Single_Cycle_Datapath (
  output [2:0] pc,
  output [8:0] Jump_Target,
  output [11:0] Jump_Address,
  output [11:0] Data_1,
  output [11:0] Data_2,
  output [11:0] Data_For_Store,
  output [11:0] Result_Value,
  output [2:0] rt,
  output [2:0] rs,
  output j,
  output [2:0] rd,
  output [2:0] opcode
);

  wire Clk_out, cu_1_a_inv, cu_1_alu_src, cu_1_enable, cu_1_lw, cu_1_ram_to_reg, cu_1_reg_dst, cu_1_sub,
       cu_1_sw, n12_bit_alu_1_cout, n12_bit_alu_1_overflow, n12_bit_alu_1_zero, or_1_out;
  wire [1:0] cu_1_out_5;
  wire [2:0] multiplexer_2_out;
  wire [8:0] adder_1_out;
  wire [11:0] bit_extender_1_out, multiplexer_1_out, n12_bit_alu_1_out_7, PC_q, ram_1_data;

  Multiplexer #(.width(12), .enable("false")) multiplexer_1 (
    .in0({Jump_Address[11:9], adder_1_out}), .in1(Jump_Address), .out(multiplexer_1_out), .sel(j));
  Register #(.width(12)) u_PC (.D(multiplexer_1_out), .Q(PC_q), .clk(Clk_out));  // open: en, clr
  Clock Clk (.out(Clk_out));
  Adder #(.width(12)) adder_1 (.a(PC_q), .b(12'h1), .out({Jump_Address[11:9], adder_1_out}));  // open: cin, cout
  cu cu_1 (
    .in_1(opcode), .reg_dst(cu_1_reg_dst), .enable(cu_1_enable), .alu_src(cu_1_alu_src), .sub(cu_1_sub),
    .a_inv(cu_1_a_inv), .sw(cu_1_sw), .lw(cu_1_lw), .ram_to_reg(cu_1_ram_to_reg), .j(j), .out_5(cu_1_out_5));
  ROM #(.addrWidth(12), .dataWidth(12)) rom_1 (.addr(PC_q), .data({opcode, Jump_Address[8:0]}));  // open: sel
  Multiplexer #(.width(3), .enable("false")) multiplexer_2 (
    .in0(Jump_Address[2:0]), .in1(Jump_Address[8:6]), .out(multiplexer_2_out), .sel(cu_1_reg_dst));
  assign bit_extender_1_out = {{9{1'b0}}, Jump_Address[2:0]};  // Bit_Extender bit_extender_1
  _12_bit_Register u_12_bit_register_1 (
    .Write_Enable(cu_1_enable), .Write_Data(Result_Value), .CLK(Clk_out), .RD(Jump_Address[8:6]),
    .out_7(Data_1), .RS(Jump_Address[5:3]), .RT(multiplexer_2_out), .out_8(Data_For_Store));
  Multiplexer #(.width(12), .enable("false")) multiplexer_3 (
    .in0(Data_For_Store), .in1(bit_extender_1_out), .out(Data_2), .sel(cu_1_alu_src));
  _12_bit_Alu u_12_bit_alu_1 (
    .A(Data_1), .out_7(n12_bit_alu_1_out_7), .Op(cu_1_out_5), .B(Data_2), .Zero(n12_bit_alu_1_zero),
    .OverFlow(n12_bit_alu_1_overflow), .A_inv(cu_1_a_inv), .B_inv(cu_1_sub), .Cin(cu_1_sub),
    .Cout(n12_bit_alu_1_cout));
  LED led_1 (.in(n12_bit_alu_1_overflow));
  LED led_2 (.in(n12_bit_alu_1_zero));
  LED led_3 (.in(n12_bit_alu_1_cout));
  or or_1 (or_1_out, cu_1_sw, cu_1_lw);
  RAM #(.addrWidth(12), .dataWidth(12), .bus("separate")) ram_1 (
    .addr(n12_bit_alu_1_out_7), .din(Data_For_Store), .data(ram_1_data), .str(cu_1_sw), .sel(or_1_out),
    .clk(Clk_out), .ld(cu_1_lw));  // open: clr
  Multiplexer #(.width(12), .enable("false")) multiplexer_4 (
    .in0(n12_bit_alu_1_out_7), .in1(ram_1_data), .out(Result_Value), .sel(cu_1_ram_to_reg));

  assign Jump_Target = Jump_Address[8:0];
  assign pc = Jump_Address[11:9];
  assign rd = Jump_Address[8:6];
  assign rs = Jump_Address[5:3];
  assign rt = Jump_Address[2:0];

  // Notes on the sheet:
  //   ROM
  //   contents of rom_1 (hex, n*v repeats v):
  //   a 2e5 5bb 60c 89d b2e dc1 e02
  //   RAM
endmodule
